// Logisim project TP1.circ as structural Verilog
module FA_1 (
  input  A,
  input  B,
  input  C1,
  output S,
  output Cout
);

  wire and_1_out, and_2_out, or_1_out, xor_1_out, xor_2_out;

  xor xor_1 (xor_1_out, A, B);
  xor xor_2 (xor_2_out, xor_1_out, C1);
  and and_1 (and_1_out, xor_1_out, C1);
  and and_2 (and_2_out, A, B);
  or or_1 (or_1_out, and_1_out, and_2_out);
endmodule

module FA_32 (
);

  wire [1:0] undriven, undriven_2;

  FA_1 fa_1_1 ();  // open: A, B, S, C1, Cout
  FA_1 fa_1_2 ();  // open: A, B, S, C1, Cout
  FA_1 fa_1_3 ();  // open: A, B, S, C1, Cout
  FA_1 fa_1_4 ();  // open: A, B, S, C1, Cout
  FA_1 fa_1_5 ();  // open: A, B, S, C1, Cout
  FA_1 fa_1_6 ();  // open: A, B, S, C1, Cout
  // Pins of 1 and 2 bits meet at undriven_2
  // Pins of 1 and 2 bits meet at undriven
endmodule
